// Logisim project control_logic.circ as structural Verilog: 1 circuit, main circuit control_logic
module control_logic (
  input  [31:0] inst,
  input  BrEq,
  input  BrLt,
  output PCSel,
  output RegWEn,
  output [2:0] ImmSel,
  output BrUn,
  output ASel,
  output BSel,
  output [3:0] ALUSel,
  output MemRW,
  output [1:0] WBSel,
  output CSRSel,
  output CSRWen
);

  wire add, add_mul_sub, andd, I_Type, mul, mulh, mulhu, not_5_out, not_6_out, not_7_out, not_8_out,
       not_9_out, not_10_out, not_11_out, not_12_out, not_13_out, not_14_out, not_15_out, orr, sll_mulh,
       slll, slt, sraa, srl_sra, srll, sub, xorr;

  Demultiplexer #(.enable("false"), .select(5)) demultiplexer_1 (
    .out4(I_Type), .out12(RegWEn), .sel(inst[6:2]));  // open: out0, out1, out2, out3, out5, out6, out7, out8, out9, out10, out11, out13, out14, out15, out16, out17, out18, out19, out20, out21, out22, out23, out24, out25, out26, out27, out28, out29, out30, out31, in
  not not_1 (ASel, RegWEn);
  not not_2 (BSel, RegWEn);
  Demultiplexer #(.enable("false"), .select(3)) demultiplexer_2 (
    .out0(add_mul_sub), .out1(sll_mulh), .out2(slt), .out3(mulhu), .out4(xorr), .out5(srl_sra), .out6(orr),
    .out7(andd), .in(RegWEn), .sel(inst[14:12]));
  not not_3 (PCSel, RegWEn);
  not not_4 (MemRW, RegWEn);
  assign WBSel = {{1{1'b0}}, RegWEn};  // Bit_Extender bit_extender_1
  Demultiplexer #(.enable("false"), .select(2)) demultiplexer_3 (
    .out0(add), .out1(mul), .out2(sub), .in(add_mul_sub), .sel({inst[30], inst[25]}));  // open: out3
  not not_5 (not_5_out, mul);
  not not_6 (not_6_out, sub);
  and and_1 (ALUSel[3], ~add, ~not_5_out, ~not_6_out, ~slll, ~not_7_out, ~slt, ~not_8_out, ~andd, ~orr, ~srll, ~sraa, ~xorr);  // AND_Gate
  not not_7 (not_7_out, mulh);
  not not_8 (not_8_out, mulhu);
  not not_9 (not_9_out, slll);
  and and_2 (ALUSel[2], ~add, ~mul, ~sub, ~not_9_out, ~mulh, ~not_10_out, ~mulhu, ~andd, ~orr, ~not_11_out, ~not_12_out, ~xorr);  // AND_Gate
  not not_10 (not_10_out, slt);
  not not_11 (not_11_out, srll);
  not not_12 (not_12_out, sraa);
  Demultiplexer #(.enable("false")) demultiplexer_4 (.out0(slll), .out1(mulh), .in(sll_mulh), .sel(inst[25]));
  and and_3 (ALUSel[1], ~add, ~mul, ~sub, ~slll, ~mulh, ~slt, ~mulhu, ~andd, ~not_13_out, ~srll, ~sraa, ~not_14_out);  // AND_Gate
  not not_13 (not_13_out, orr);
  not not_14 (not_14_out, xorr);
  and and_4 (ALUSel[0], ~add, ~mul, ~sub, ~slll, ~mulh, ~slt, ~mulhu, ~not_15_out, ~orr, ~srll, ~sraa, ~xorr);  // AND_Gate
  not not_15 (not_15_out, andd);
  Demultiplexer #(.enable("false")) demultiplexer_5 (.out0(srll), .out1(sraa), .in(srl_sra), .sel(inst[30]));

  // Other names for the same wires on the sheet: func7low = inst[25]; func7high = inst[30]; R_Type = RegWEn

  // Notes on the sheet:
  //   INPUTS to your circuit
  //   R-Type
  //   DON'T CHANGE THE LOCATIONS OF THE INPUTS AND OUTPUTS!
  //   OUTPUT from your circuit
  //   add/mul/sub
  //   and
  //   sll/mulh
  //   or
  //   slt
  //   srl/sra
  //   mulhu
  //   xor
endmodule
